# Fritzing sketch ESP8266-BME280-Blynk-DeepSleepMode-w-DI-r2 (saved by Fritzing 0.9.3b)
breadboards: 1

parts:
  R1 = Resistor [tolerance=±5% resistance=220 package=THT]
  C1 = Electrolytic Capacitor [capacitance=1µF package="100 mil [THT, electrolytic]"]
  Temprature_Humidity_Pressure1 = AM-BME280
  W1 = ESPr Developer [package="DIP (Dual Inline) [THT]"]
  VCC1 = 4 x AAA Battery Mount

nets:
  N1: R1.Pin_0, C1.-, Temprature_Humidity_Pressure1.SDO, Temprature_Humidity_Pressure1.GND, W1.GND#9, VCC1.-
  N2: R1.Pin_1, W1.RST, W1.IO16
  N3: C1.+, W1.VIN, VCC1.+
  N4: Temprature_Humidity_Pressure1.SCK, W1.IO5
  N5: Temprature_Humidity_Pressure1.SDI, W1.IO4
  VDD: Temprature_Humidity_Pressure1.VDD, W1.3V3

custom parts:
  AM-BME280: Akitsukitusho AM-BME280
